# Fritzing sketch ESQUEMATICOSTD3 (saved by Fritzing 0.9.6b)
breadboards: 1

parts:
  M1 = STM32F103C8T6 blue mini board
  U1 = MCP2562 CAN Transceiver [part_number=MCP2551 package="DIP8 [THT]"]
  R_VERDE = Resistor [tolerance=±1% resistance=0 package="2512 [SMD]"]
  LED1 = smd LED [color="Red (633nm)" package="0805 [SMD]"]
  R2 = Resistor [tolerance=±5% resistance=100 package="2512 [SMD]"]
  R3 = Resistor [tolerance=±5% resistance=4.7k package="2512 [SMD]"]
  R4 = Resistor [tolerance=±5% resistance=4.7k package="2512 [SMD]"]
  R6 = Resistor [tolerance=±5% resistance=10k package="2512 [SMD]"]
  JP1 = Header 1 [package=luxeon-pad]
  CN5 = Header 10 [package=1x10-2mm-smd]
  CN2 = JST-VHR-3N [part_number=JST-VHR-3N package=THT]
  CN1 = Header 5 [package=1x05-1mm]
  CN4 = JST-VHR-3N [part_number=JST-VHR-3N package=THT]
  CN3 = JST-VHR-3N [part_number=JST-VHR-3N package=THT]
  JP2 = Header 1 [package=luxeon-pad]
  CN6 = Header 12 [package=1x12_machine-pin-header_lock.004]
  CN7 = Header 6 [package=1x06_smd_straight_alt]
  R7 = Resistor [tolerance=±5% resistance=4.7k package="2512 [SMD]"]
  R8 = Resistor [tolerance=±5% resistance=4.7k package="2512 [SMD]"]
  R9 = Resistor [tolerance=±5% resistance=4.7k package="2512 [SMD]"]
  R10 = Resistor [tolerance=±5% resistance=4.7k package="2512 [SMD]"]
  R11 = Resistor [tolerance=±5% resistance=4.7k package="2512 [SMD]"]
  R12 = Resistor [tolerance=±5% resistance=4.7k package="2512 [SMD]"]
  R_NEGRO = Resistor [tolerance=±1% resistance=1k package="2512 [SMD]"]
  JP3 = Header 1 [package=luxeon-pad]
  JP4 = Header 1 [package=luxeon-pad]
  R_ROJO2 = Resistor [tolerance=±5% resistance=220 package="2512 [SMD]"]
  JP5 = Header 1 [package=luxeon-pad]
  JP6 = Header 1 [package=luxeon-pad]
  R_AMARILLO = Resistor [tolerance=±1% resistance=0 package="2512 [SMD]"]
  JP7 = Header 1 [package=luxeon-pad]
  JP8 = Header 1 [package=luxeon-pad]
  R_AZUL = Resistor [tolerance=±5% resistance=33k package="2512 [SMD]"]
  JP9 = Header 1 [package=luxeon-pad]
  JP10 = Header 1 [package=luxeon-pad]
  R_ROJO1 = Resistor [tolerance=±5% resistance=2.2k package="2512 [SMD]"]
  R_BLANCO1 = Resistor [tolerance=±5% resistance=220k package="2512 [SMD]"]
  R_BLANCO2 = Resistor [tolerance=±5% resistance=100k package="2512 [SMD]"]
  JP11 = Header 1 [package=luxeon-pad]
  JP12 = Header 1 [package=luxeon-pad]
  P4 = JST-VHR-3N [part_number=JST-VHR-3N package=THT]
  P5 = Header 10 [package=1x10-2mm-smd]

nets:
  N1: M1.A9, R4.Pin_0
  N2: M1.A10, CN2.pin2, CN2.pin_5
  N3: M1.B8, R3.Pin_0
  N4: M1.B9, U1.connector0
  5V: M1.5V, CN1.5
  N5: M1.A0, CN5.4
  N6: M1.A1, CN5.5
  N7: M1.A2, CN5.6
  N8: M1.A3, CN5.7
  N9: M1.A4, CN5.8
  N10: M1.A5, CN5.9
  N11: M1.B11, R2.Pin_0
  GND: M1.G, M1.GND, U1.connector1, R6.Pin_1, CN2.pin_6, CN4.pin3, CN4.pin_5, CN4.pin_4, CN4.pin_6, CN7.1, CN7.2, CN7.3, CN7.4, CN7.5, CN7.6, P4.pin2, P4.pin1, P4.pin_5, P4.pin_4, P4.pin_6
  3.3V: U1.connector2, LED1.anode, CN5.1, CN5.2, CN3.pin2, CN3.pin_5, R7.Pin_1, R8.Pin_1, R9.Pin_1, R10.Pin_1, R11.Pin_1, R12.Pin_1, P5.8, P5.9
  N12: U1.connector3, R3.Pin_1
  N13: U1.connector5, CN1.4
  N14: U1.connector6, CN1.3
  N15: U1.connector7, R6.Pin_0, CN1.2
  N16: R_VERDE.Pin_0, JP2.1
  N17: R_VERDE.Pin_1, JP1.1
  N18: LED1.cathode, R2.Pin_1, CN3.pin1, CN3.pin_4
  N19: R4.Pin_1, CN2.pin1, CN2.pin_4
  N20: CN6.1, CN6.2, R7.Pin_0, P5.1
  N21: CN6.3, CN6.4, R8.Pin_0, P5.2
  N22: CN6.5, CN6.6, R9.Pin_0, P5.3
  N23: CN6.7, CN6.8, R10.Pin_0, P5.4
  N24: CN6.9, CN6.10, R11.Pin_0, P5.5
  N25: CN6.11, CN6.12, R12.Pin_0, P5.6
  N26: R_NEGRO.Pin_0, JP4.1
  N27: R_NEGRO.Pin_1, JP3.1
  N28: R_ROJO2.Pin_0, JP6.1
  N29: R_ROJO2.Pin_1, R_ROJO1.Pin_0
  N30: JP5.1, R_ROJO1.Pin_1
  N31: R_AMARILLO.Pin_0, JP8.1
  N32: R_AMARILLO.Pin_1, JP7.1
  N33: R_AZUL.Pin_0, JP10.1
  N34: R_AZUL.Pin_1, JP9.1
  N35: R_BLANCO1.Pin_0, JP12.1
  N36: R_BLANCO1.Pin_1, R_BLANCO2.Pin_0
  N37: R_BLANCO2.Pin_1, JP11.1

notes:
  Cables
  a CN6
  a CN7
  Placa base
  Placas del frente

custom parts:
  MCP2562 CAN Transceiver: The MCP2561/2 is a Microchip Technology Inc. second generation high-speed CAN transceiver. It serves as an interface between a CAN protocol controller and the physical two-wire CAN bus. It has a VIO Supply Pin to Interface Directly to CAN Controllers and Microcontrollers with 1.8V to 5.5V I/O.
