# Fritzing sketch esq_fuente (saved by Fritzing 0.9.6b)
breadboards: 1

parts:
  U1 = LM2596 step down module
  CN1 = Hirose DF13 Series Header [part_number=DF13#-2P-1.25V package=DF13C-2P-1.25V]
  SW1 = SWITCH-MOMENTARY-2 [package=tactile-pth]
  CN2 = Header 5 [package=1x05-1mm]
  R41 = Resistor [tolerance=±5% power=0.25 resistance=220 package=THT]
  C1 = Capacitor [part_number="0.1 uF" package=0805]
  C2 = Capacitor Polarized [part_number="100 uF x 63V" package=panasonic_d]
  C3 = Capacitor [part_number="0.1 uF" package=0805]
  C4 = Capacitor Polarized [part_number="100 uF x 63V" package=panasonic_d]

nets:
  13V: U1.IN+, SW1.2, C3.1, C4.+
  GND: U1.IN-, U1.OUT-, CN1.2, CN2.4, C1.2, C2.-, C3.2, C4.-
  5V: U1.OUT+, CN2.1, C1.1, C2.+
  N1: CN1.1, SW1.1
  N2: CN2.2, R41.Pin_0
  N3: CN2.3, R41.Pin_1

custom parts:
  LM2596 step down module: LM2596 DC-DC step down power supply module 3 A.
