# Fritzing sketch esq_password (saved by Fritzing 0.9.6b)
breadboards: 1

parts:
  M1 = STM32F103C8T6 blue mini board
  U1 = MCP2562 CAN Transceiver [part_number=MCP2551 package="DIP8 [THT]"]
  LED1 = smd LED [color="Red (633nm)" package="0805 [SMD]"]
  R2 = Resistor [tolerance=±5% resistance=100 package="2512 [SMD]"]
  R1 = Resistor [tolerance=±5% resistance=4.7k package="2512 [SMD]"]
  R3 = Resistor [tolerance=±5% resistance=10k package="2512 [SMD]"]
  CN1 = Header 5 [package=1x05-1mm]
  CN2 = JST-VHR-3N [package=THT]
  R4 = Resistor [tolerance=±5% power=0.25 resistance=15k package=THT]
  R5 = Resistor [tolerance=±5% power=0.25 resistance=15k package=THT]
  C1 = Capacitor [part_number="1 uF" package=0805]
  C2 = Capacitor [part_number="1 uF" package=0805]
  S1 = Momentary Switch [package=tactile_switch_smd]
  S2 = Momentary Switch [package=tactile_switch_smd]
  U2 = OLED Mono 0.56 inch blue or white
  CN3 = polarizedheader 4pin 0.156in [package=THT]
  CN3_2 = Header 5 [package=1x05-1mm]
  R6 = Resistor [tolerance=±5% power=0.25 resistance=15k package=THT]
  R7 = Resistor [tolerance=±5% power=0.25 resistance=15k package=THT]
  C3 = Capacitor [part_number="1 uF" package=0805]
  C4 = Capacitor [part_number="1 uF" package=0805]
  S3 = Momentary Switch [package=tactile_switch_smd]
  S4 = Momentary Switch [package=tactile_switch_smd]
  R8 = Resistor [tolerance=±5% power=0.25 resistance=15k package=THT]
  R9 = Resistor [tolerance=±5% power=0.25 resistance=15k package=THT]
  C5 = Capacitor [part_number="1 uF" package=0805]
  C6 = Capacitor [part_number="1 uF" package=0805]
  S5 = Momentary Switch [package=tactile_switch_smd]
  S6 = Momentary Switch [package=tactile_switch_smd]
  R10 = Resistor [tolerance=±5% power=0.25 resistance=15k package=THT]
  R11 = Resistor [tolerance=±5% power=0.25 resistance=15k package=THT]
  C7 = Capacitor [part_number="1 uF" package=0805]
  C8 = Capacitor [part_number="1 uF" package=0805]
  S7 = Momentary Switch [package=tactile_switch_smd]
  S8 = Momentary Switch [package=tactile_switch_smd]
  R12 = Resistor [tolerance=±5% power=0.25 resistance=15k package=THT]
  R13 = Resistor [tolerance=±5% power=0.25 resistance=15k package=THT]
  C9 = Capacitor [part_number="1 uF" package=0805]
  C10 = Capacitor [part_number="1 uF" package=0805]
  S9 = Momentary Switch [package=tactile_switch_smd]
  S10 = Momentary Switch [package=tactile_switch_smd]
  R14 = Resistor [tolerance=±5% power=0.25 resistance=15k package=THT]
  C11 = Capacitor [part_number="1 uF" package=0805]
  S12 = Momentary Switch [part_number=send package=tactile_switch_smd]
  P5 = Header 6 [package=1x06_smd_straight_combo]
  P4 = Header 10 [package=1x10-2mm-smd]
  CN6 = JST-VHR-3N [package=THT]
  CN4 = Header 10 [package=1x10-2mm-smd]  # not connected
  CN5 = Header 6 [package=1x06_smd_straight_combo]  # not connected
  R15 = Resistor [tolerance=±5% resistance=4.7k package="2512 [SMD]"]
  CN2_2 = JST-VHR-3N [package=THT]

nets:
  N1: M1.A9, R15.Pin_0
  N2: M1.A10, CN2_2.pin2, CN2_2.pin_5
  N3: M1.B6, CN3_2.1
  N4: M1.B7, CN3_2.2
  N5: M1.B8, R1.Pin_0
  N6: M1.B9, U1.connector0
  5V: M1.5V, CN1.5
  GND: M1.G, M1.GND, U1.connector1, R3.Pin_1, C1.2, C2.2, S1.1, S1.2, S2.1, S2.2, CN3_2.5, C3.2, C4.2, S3.1, S3.2, S4.1, S4.2, C5.2, C6.2, S5.1, S5.2, S6.1, S6.2, C7.2, C8.2, S7.1, S7.2, S8.1, S8.2, C9.2, C10.2, S9.1, S9.2, S10.1, S10.2, C11.2, S12.1, S12.2, P4.9, CN2_2.pin3, CN2_2.pin_6
  3.3V: M1.3.3V, U1.connector2, LED1.anode, R4.Pin_0, R5.Pin_0, CN3_2.3, R6.Pin_0, R7.Pin_0, R8.Pin_0, R9.Pin_0, R10.Pin_0, R11.Pin_0, R12.Pin_0, R13.Pin_0, R14.Pin_0, P4.8
  N7: M1.B11, R2.Pin_0
  N8: U1.connector3, R1.Pin_1
  N9: U1.connector5, CN1.4
  N10: U1.connector6, CN1.3
  N11: U1.connector7, R3.Pin_0, CN1.2
  N12: LED1.cathode, CN6.pin1, CN6.pin_4
  N13: R2.Pin_1, CN2.pin1, CN2.pin_4
  up 1 .: R4.Pin_1, C1.1, S1.3, S1.4
  up 2 .: R5.Pin_1, C2.1, S2.3, S2.4
  N14: U2.SDA, CN3.pin3
  N15: U2.SCL, CN3.pin4
  N16: U2.VCC, CN3.pin1
  N17: U2.GND, CN3.pin2
  up 3 .: R6.Pin_1, C3.1, S4.3, S4.4
  up 4 .: R7.Pin_1, C4.1, S3.3, S3.4
  up 5 .: R8.Pin_1, C5.1, S6.3, S6.4
  dw 1 .: R9.Pin_1, C6.1, S5.3, S5.4
  dw 2 .: R10.Pin_1, C7.1, S8.3, S8.4
  dw 3 .: R11.Pin_1, C8.1, S7.3, S7.4
  dw 4 .: R12.Pin_1, C9.1, S10.3, S10.4
  dw 5 .: R13.Pin_1, C10.1, S9.3, S9.4
  N18: R14.Pin_1, C11.1, S12.3, S12.4, CN6.pin_5
  dw 1: P5.1
  dw 2: P5.3
  dw 3: P5.4
  dw 4: P5.5
  dw 5: P5.6
  up 1: P4.1
  up 2: P4.3
  up 3: P4.4
  up 4: P4.5
  up 5: P4.6
  N19: R15.Pin_1, CN2_2.pin1, CN2_2.pin_4

notes:
  Placa base
  Display
  Pulsadores ascendentes
  Pulsadores descendentes
  Enviar y strike

custom parts:
  MCP2562 CAN Transceiver: The MCP2561/2 is a Microchip Technology Inc. second generation high-speed CAN transceiver. It serves as an interface between a CAN protocol controller and the physical two-wire CAN bus. It has a VIO Supply Pin to Interface Directly to CAN Controllers and Microcontrollers with 1.8V to 5.5V I/O.
  OLED Mono 0.56 inch blue or white: OLED, I2C 3.3V - 5V Blue and White text versions
