# Fritzing sketch esq_placaCentral (saved by Fritzing 0.9.6b)
breadboards: 1

parts:
  M1 = STM32F103C8T6 blue mini board
  U1 = MCP2562 CAN Transceiver [part_number=MCP2551 package="DIP8 [THT]"]
  R3 = Resistor [tolerance=±5% resistance=4.7k package="2512 [SMD]"]
  R6 = Resistor [tolerance=±5% resistance=10k package="2512 [SMD]"]
  CN4 = Header 10 [package=1x10-2mm-smd]
  CN1 = Header 5 [package=1x05-1mm]
  U3 = OLED Mono 0.56 inch blue or white
  CN7 = Header 10 [package=1x10-2mm-smd]
  CN3 = polarizedheader 4pin 0.156in [package=THT]
  CN5 = polarizedheader 4pin 0.156in [package=THT]
  CN6 = Header 8 [package=1x08_smd_combined]
  CN9 = Header 8 [package=1x08_smd_combined]
  LED1 = LED - 5mm [color="Red (633nm)" current=0.030 package="5 mm [THT]"]
  LED2 = LED - 5mm [color="Red (633nm)" current=0.030 package="5 mm [THT]"]
  LED3 = LED - 5mm [color="Red (633nm)" current=0.030 package="5 mm [THT]"]
  R17 = Resistor [tolerance=±5% power=0.25 resistance=220 package=THT]
  R18 = Resistor [tolerance=±5% power=0.25 resistance=220 package=THT]
  R19 = Resistor [tolerance=±5% power=0.25 resistance=220 package=THT]
  SW1 = SWITCH-MOMENTARY-2 [package=tactile-pth]
  C1 = Capacitor [package=0805]
  R20 = Resistor [tolerance=±5% power=0.25 resistance=220 package=THT]
  SWRST = SWITCH-MOMENTARY-2 [package=tactile-pth]
  Q1 = PNP-Transistor [part_number=BC558 package="TO92 [THT]"]
  Q2 = PNP-Transistor [part_number=BC558 package="TO92 [THT]"]
  Q3 = PNP-Transistor [part_number=BC558 package="TO92 [THT]"]
  Q4 = PNP-Transistor [part_number=BC558 package="TO92 [THT]"]
  R21 = Resistor [tolerance=±5% power=0.25 resistance=4.7k package=THT]
  R22 = Resistor [tolerance=±5% power=0.25 resistance=4.7k package=THT]
  R23 = Resistor [tolerance=±5% power=0.25 resistance=4.7k package=THT]
  R24 = Resistor [tolerance=±5% power=0.25 resistance=4.7k package=THT]
  CN8 = polarizedheader 4pin 0.156in [package=THT]
  CN2 = polarizedheader 4pin 0.156in [package=THT]
  LED4 = 7-SEGMENT-4DIGIT-YOUNGSUN [package=7-segment-4digit-youngsun]
  R33 = Resistor [tolerance=±5% resistance=220 package="2512 [SMD]"]
  R34 = Resistor [tolerance=±5% resistance=220 package="2512 [SMD]"]
  R35 = Resistor [tolerance=±5% resistance=220 package="2512 [SMD]"]
  R36 = Resistor [tolerance=±5% resistance=220 package="2512 [SMD]"]
  R37 = Resistor [tolerance=±5% resistance=220 package="2512 [SMD]"]
  R38 = Resistor [tolerance=±5% resistance=220 package="2512 [SMD]"]
  R39 = Resistor [tolerance=±5% resistance=220 package="2512 [SMD]"]
  R40 = Resistor [tolerance=±5% resistance=220 package="2512 [SMD]"]

nets:
  D4: M1.B12, R21.Pin_0
  D3: M1.B13, R24.Pin_0
  D2: M1.B14, R22.Pin_0
  D1: M1.B15, R23.Pin_0
  N1: M1.B6, CN3.pin4
  N2: M1.B7, CN3.pin3
  N3: M1.B8, R3.Pin_0
  N4: M1.B9, U1.connector0
  5V: M1.5V, CN1.5
  GND: M1.G, M1.GND, U1.connector1, R6.Pin_1, CN3.pin2, CN6.6
  3.3V: M1.3.3V, U1.connector2, CN3.pin1, CN6.7, R17.Pin_1, R18.Pin_1, R19.Pin_1, Q1.E, Q2.E, Q3.E, Q4.E, LED4.COL-A
  N5: M1.A0, R33.Pin_1
  N6: M1.A1, R34.Pin_1
  N7: M1.A2, R35.Pin_1
  N8: M1.A3, R36.Pin_1
  N9: M1.A4, R37.Pin_1
  N10: M1.A5, R38.Pin_1
  N11: M1.A6, R39.Pin_1
  N12: M1.A7, R40.Pin_1
  N13: M1.B0, CN6.1
  N14: M1.B1, CN6.2
  N15: M1.B10, CN6.3
  N16: M1.B11, CN6.4
  N17: M1.RST, CN6.5
  N18: U1.connector3, R3.Pin_1
  N19: U1.connector5, CN1.4
  N20: U1.connector6, CN1.3
  N21: U1.connector7, R6.Pin_0, CN1.2
  N22: CN4.1, R33.Pin_0
  N23: CN4.2, R34.Pin_0
  N24: CN4.3, R35.Pin_0
  N25: CN4.4, R36.Pin_0
  N26: CN4.5, R37.Pin_0
  N27: CN4.6, R38.Pin_0
  N28: CN4.7, R39.Pin_0
  N29: CN4.8, R40.Pin_0
  N30: U3.SDA, CN5.pin3
  N31: U3.SCL, CN5.pin4
  N32: U3.VCC, CN5.pin1
  N33: U3.GND, CN5.pin2
  N34: CN7.1, LED4.COL-C
  N35: CN7.2, LED4.A
  N36: CN7.3, LED4.B
  N37: CN7.4, LED4.C
  N38: CN7.5, LED4.D
  N39: CN7.6, LED4.E
  N40: CN7.7, LED4.F
  N41: CN7.8, LED4.G
  N42: CN9.1, LED1.cathode
  N43: CN9.2, LED3.cathode
  N44: CN9.3, LED2.cathode
  N45: CN9.4, SW1.2, C1.1, R20.Pin_1
  N46: CN9.5, SWRST.2
  N47: CN9.6, SW1.1, C1.2, SWRST.1
  N48: CN9.7, R20.Pin_0
  N49: LED1.anode, R17.Pin_0
  N50: LED2.anode, R19.Pin_0
  N51: LED3.anode, R18.Pin_0
  N52: Q1.B, R23.Pin_1
  N53: Q1.C, CN2.pin1
  N54: Q2.B, R22.Pin_1
  N55: Q2.C, CN2.pin2
  N56: Q3.B, R21.Pin_1
  N57: Q3.C, CN2.pin3
  N58: Q4.B, R24.Pin_1
  N59: Q4.C, CN2.pin4
  N60: CN8.pin1, LED4.DIG1
  N61: CN8.pin2, LED4.DIG2
  N62: CN8.pin3, LED4.DIG3
  N63: CN8.pin4, LED4.DIG4

notes:
  Placa base
  Displays
  Pulsadores y LEDs

custom parts:
  MCP2562 CAN Transceiver: The MCP2561/2 is a Microchip Technology Inc. second generation high-speed CAN transceiver. It serves as an interface between a CAN protocol controller and the physical two-wire CAN bus. It has a VIO Supply Pin to Interface Directly to CAN Controllers and Microcontrollers with 1.8V to 5.5V I/O.
  OLED Mono 0.56 inch blue or white: OLED, I2C 3.3V - 5V Blue and White text versions
