# Fritzing sketch placaRobot (saved by Fritzing 0.9.6b)
perfboards: 4

parts:
  LLC1 = Logic Level Converter [package="Breakout board"]
  J1 = Camdenboss CTB0158-2 [part_number=CTB0158-2 package=THT]  # not connected
  J2 = Camdenboss CTB0158-2 [part_number=CTB0158-2 package=THT]
  HC-SR04_Sensor_1 = HC-SR04 Ultrasonic Distance Sensor  # not connected
  M1 = STM32F103C8T6 blue mini board
  J3 = Camdenboss CTB0158-2 [part_number=CTB0158-2 package=THT]  # not connected

nets:
  N1: LLC1.LV1, M1.A6
  N2: LLC1.LV2, M1.A5
  N3: LLC1.L-GND, LLC1.H-GND
  N4: LLC1.LV3, M1.A1
  N5: LLC1.LV4, M1.A0
  N6: LLC1.HV, J2.pin1, J2.terminal_1
  N7: J2.pin2, M1.G, M1.GND

custom parts:
  Logic Level Converter: 5V to/from 3.3V logic level converter
