# Fritzing sketch placaVentiladorRele (saved by Fritzing 0.9.6b)
perfboards: 1

parts:
  Mod1 = Amica NodeMCU DevKit 1.0
  U1 = 4-Channel 5v Relay Shield [package=relay-4ch5v10a]  # not connected
  Q1 = 2N7000 FET N-Channel [part_number=2N7000 package=TO92]  # not connected
  Q2 = 2N7000 FET N-Channel [part_number=2N7000 package=TO92]  # not connected
  Q3 = 2N7000 FET N-Channel [part_number=2N7000 package=TO92]  # not connected
  Q4 = 2N7000 FET N-Channel [part_number=2N7000 package=TO92]  # not connected
  R1 = Resistor [tolerance=±5% power=0.25 resistance=22k package=THT]
  R3 = Resistor [tolerance=±5% power=0.25 resistance=22k package=THT]
  R4 = Resistor [tolerance=±5% power=0.25 resistance=22k package=THT]
  R2 = Resistor [tolerance=±5% power=0.25 resistance=22k package=THT]
  J1 = female pin header, 2 pins [form="♀ (female)"]
  J2 = female pin header, 2 pins [form="♀ (female)"]
  J3 = female pin header, 2 pins [form="♀ (female)"]

nets:
  N1: Mod1.pin1, Mod1.pin_10, Mod1.pin_26
  N2: Mod1.pin2, Mod1.pin_9, Mod1.pin_25, Mod1.pin_29, J1.pin1
  N3: Mod1.pin_30, R1.Pin_0, R3.Pin_1, R4.Pin_1, R2.Pin_0, J3.pin2
  N4: R1.Pin_1, J1.pin2
  N5: R3.Pin_0, J2.pin2
  N6: R4.Pin_0, J3.pin1
  N7: R2.Pin_1, J2.pin1

custom parts:
  Amica NodeMCU DevKit 1.0: Amica NodeMCU DevKit 1.0 Development Kit based on ESP8266 ESP-12E, integating GPIO, PWM, IIC, 1-Wire and ADC all in one board. Links: NodeMCU information page Github
  4-Channel 5v Relay Shield: 4 Channel 5v Relay Shield w. 2x SPD-06VDC-SD-C
  2N7000 FET N-Channel: A 2N7000 MOSFET N-Channel Transistor
